# Fritzing sketch SoDoNguyenLi (saved by Fritzing 0.9.5d)
breadboards: 3

parts:
  A1 = ESP32-S3 devkit 1
  RHT1 = Humidity and Temperature Sensor RHT03
  LED1 = Green LED - Rect 5x2x7mm [package="5x2x7 mm [THT]"]
  LED2 = Green LED - Rect 5x2x7mm [package="5x2x7 mm [THT]"]
  LED3 = Green LED - Rect 5x2x7mm [package="5x2x7 mm [THT]"]
  LED4 = Red LED - Rect 5x2x7mm [package="5x2x7 mm [THT]"]  # not connected
  R1 = Resistor [tolerance=±5% resistance=220 package="0603 [SMD]"]
  R2 = Resistor [tolerance=±5% resistance=220 package="0603 [SMD]"]
  R3 = Resistor [tolerance=±5% resistance=220 package="0603 [SMD]"]
  R4 = Resistor [tolerance=±5% resistance=10k package="0603 [SMD]"]
  Part1 = HC-SR501 Body Sensor Module
  U1 = GAS_SENSOR [package=mq-3]
  R5 = Photocell (LDR) [package=THT]
  Grove1 = Grove OLED 128x96
  Part2 = INMP441
  Part3 = InvenSense MPU6050
  Bat1 = battery_holder_single_18650
  Bat2 = battery_holder_single_18650
  M1 = RioRand LM2596
  J2 = Piezo Speaker
  A2 = Arducam mini 2mp plus pins swapped
  U2 = RFID RC522 SIP - 8 pins [chip_label="RFID RC522" package="SIP (Single Inline) [THT]"]
  J1 = Basic Servo
  R6 = Resistor [tolerance=±5% resistance=10000 package=THT]
  R7 = Resistor [tolerance=±5% resistance=10k package="0603 [SMD]"]
  J3 = Piezo Speaker
  R8 = Resistor [tolerance=±5% resistance=220 package="0603 [SMD]"]
  R9 = Resistor [tolerance=±5% resistance=220 package="0603 [SMD]"]
  R10 = Resistor [tolerance=±5% resistance=220 package="0603 [SMD]"]

nets:
  GND: A1.Pin_1, A1.Pin_42, RHT1.GND_2, LED1.cathode, LED2.cathode, LED3.cathode, R4.Pin_0, Part1.GND, U1.H1, Grove1.GND, Part2.L/R, Part2.GND, Part3.GND, Part3.AD0, M1.Pin_4, J2.pin1, A2.Pin_4, U2.GND, J1.gnd, R6.Pin_1, J3.pin1
  VCC: A1.Pin_2, A1.Pin_21, RHT1.Vcc, R5.pin_0, Grove1.VCC, Part3.VCC, A2.Pin_3, U2.VCC, R7.Pin_0, J3.pin2
  N1: A1.Pin_4, U1.B1, R6.Pin_0
  N2: A1.Pin_6, Grove1.SCL, Part3.SCL, A2.Pin_1
  N3: A1.Pin_7, Grove1.SDA, Part3.SDA, A2.Pin_2
  N4: A1.Pin_12, R3.Pin_1
  N5: A1.Pin_18, Part2.SD
  N6: A1.Pin_19, Part2.SCK
  N7: A1.Pin_20, Part2.WS
  VCC_2: A1.Pin_22, Part1.VCC, U1.A1, U1.H2, Part2.VDD, M1.Pin_3, J1.vcc
  N8: A1.Pin_23, R1.Pin_1
  N9: A1.Pin_24, R2.Pin_1
  N10: A1.Pin_25, R9.Pin_1
  N11: A1.Pin_26, R10.Pin_1
  N12: A1.Pin_27, R8.Pin_1
  N13: A1.Pin_28, R4.Pin_1, R5.pin_1
  N14: A1.Pin_29, Part1.OUT
  N15: A1.Pin_32, U2.RST
  N16: A1.Pin_33, A2.Pin_7, U2.MOSI
  N17: A1.Pin_34, A2.Pin_6, U2.MISO
  N18: A1.Pin_35, A2.Pin_5, U2.SCK
  N19: A1.Pin_36, U2.NSS
  N20: A1.Pin_37, RHT1.Data-signal, R7.Pin_1
  N21: LED1.anode, R1.Pin_0
  N22: LED2.anode, R2.Pin_0
  N23: LED3.anode, R9.Pin_0
  N24: Bat1.+#0, M1.Pin_1
  N25: Bat1.+#1, Bat2.+#0
  N26: Bat2.+#1, M1.Pin_2
  N27: J2.pin2, R8.Pin_0

custom parts:
  ESP32-S3 devkit 1: ESP32-S3-DevKitC-1 Development Board BT 2.4G Wifi Module for Arduino 8MB PSRAM 16MB FLASH N16R8 42Pin CH340C Type-C ESP32 S3.
  Green LED - Rect 5x2x7mm: A generic rectangular green LED (~1.8V) 5mm x 2mm x 7mm
  Red LED - Rect 5x2x7mm: A generic rectangular red LED (~1.8V) 5mm x 2mm x 7mm
  HC-SR501 Body Sensor Module: Pyroelectric Infrared PIR Motion Sensor Detector Module
  INMP441: This is a simple breakout board for the INMP441 I2S MEMS microphone.
  battery_holder_single_18650: single 18650 battery holder
  Arducam mini 2mp plus pins swapped: ArduCAM-2MP-Plus is a high-definition 2MP SPI camera, which reduces the complexity of the camera control interface.This version is from the back of the board.
  RFID RC522 SIP - 8 pins: A SIP stand-in part for RFID RC522 . With 8 pins on a 300 mil single inline package (SIP) footprint.
